# Fritzing sketch schema (saved by Fritzing 1.0.2b)
breadboards: 1

parts:
  Composant1 = Arduino Uno (Rev3) - ICSP
  J1 = Basic Servo
  HC-SR04_Sensor_1 = HC-SR04 Ultrasonic Distance Sensor
  LED1 = smd LED [color="Red (633nm)" package="0603 [SMD]"]
  LED2 = smd LED [color="Green (565nm)" package="0603 [SMD]"]
  R1 = Resistor [tolerance=±5% power=0.25W resistance=470 package=THT]
  R2 = Resistor [tolerance=±5% power=0.25W resistance=470 package=THT]
  C1 = Electrolytic Capacitor [capacitance=1mF voltage=35V package="200 mil [THT, electrolytic]"]

nets:
  VCC: Composant1.5V, J1.vcc, HC-SR04_Sensor_1.VCC, C1.+
  GND: Composant1.GND, J1.gnd, HC-SR04_Sensor_1.GND, R1.Pin_0, R2.Pin_0, C1.-
  N1: Composant1.D9_PWM, J1.pulse
  N2: Composant1.D10_PWM/SS, LED2.anode
  N3: Composant1.D11_PWM/MOSI, LED1.anode
  N4: Composant1.D3_PWM, HC-SR04_Sensor_1.ECHO
  N5: Composant1.D4, HC-SR04_Sensor_1.TRIG
  N6: LED1.cathode, R2.Pin_1
  N7: LED2.cathode, R1.Pin_1
